# Fritzing sketch ESP32_IoT_House_COMPLETE (saved by Fritzing 0.8.7b)
breadboards: 5

parts:
  U1 = ESP32-38PinWide [part_number=ESP32-38PinWide]
  BME-280 = BME280
  OLED_128x64_I2C_-_1 = OLED 128x64 I2C Monochrome Display
  R4 = Resistor [tolerance=±1% resistance=330 package=THT]
  S1 = Pushbutton [package="[THT]"]
  S2 = Pushbutton [package="[THT]"]
  R6 = Resistor [tolerance=±1% resistance=10k package=THT]
  R5 = Resistor [tolerance=±1% resistance=10k package=THT]
  C1 = Ceramic Capacitor [capacitance=100nF package="200 mil [THT, multilayer]"]
  C2 = Ceramic Capacitor [capacitance=100nF package="200 mil [THT, multilayer]"]
  Fan_12V = Fan - Ventilador [package=THT]
  Q1 = NPN-Transistor [package="TO92 [THT]"]
  R1 = Resistor [tolerance=±1% resistance=5.1k package=THT]
  9V_DC_/_5V_DC_Power_Supply = YwRobot Breadboard Power Supply [part_number=545043]
  LED2 = LED - 3mm [color="Green (555nm)" package="3 mm [THT]"]
  R3 = Resistor [tolerance=±1% resistance=330 package=THT]
  R2 = Resistor [tolerance=±1% resistance=330 package=THT]
  LED1 = LED - 3mm [color="Blue (430nm)" package="3 mm [THT]"]
  MQ-2 = MQ-3 breakout
  12V_DC_Power_Supply = PowerBRICK 12V
  J1 = Basic Servo
  Active_Buzzer_-_1 = KY-012 Active Buzzer Module [package="Breakout board"]
  Active_Buzzer_-_2 = KY-012 Active Buzzer Module [package="Breakout board"]
  OLED_128x64_I2C_-_2 = OLED 128x64 I2C Monochrome Display
  RFID_Reader/Writer = RFID RC522 Module [package=THT]
  R7 = Resistor [tolerance=±5% resistance=330 package=THT]
  U2 = ESP32-38PinWide [part_number=ESP32-38PinWide]
  LED4 = LED - 3mm [color="Red (633nm)" package="3 mm [THT]"]
  LED5 = LED - 3mm [color="Red (633nm)" package="3 mm [THT]"]
  LED6 = LED - 3mm [color="Red (633nm)" package="3 mm [THT]"]
  LED3 = LED - 3mm [color="Red (633nm)" package="3 mm [THT]"]

nets:
  N1: U1.3.3, BME-280.VIN, S1.Pin_3, S1.Pin_4, S2.Pin_3, S2.Pin_4
  N2: U1.GPIO36, MQ-2.AO
  N3: U1.GPIO32, Active_Buzzer_-_1.S
  N4: U1.GPIO25, LED3.anode
  N5: U1.GPIO26, LED2.anode
  N6: U1.GPIO27, LED1.anode
  GND: U1.GND, BME-280.GND, OLED_128x64_I2C_-_1.GND, R4.Pin_1, R6.Pin_1, R5.Pin_1, C1.0, C2.0, Q1.C, 9V_DC_/_5V_DC_Power_Supply.GND#11, R3.Pin_1, R2.Pin_1, MQ-2.GND, 12V_DC_Power_Supply.GND, J1.gnd, Active_Buzzer_-_1.-, Active_Buzzer_-_2.-, OLED_128x64_I2C_-_2.GND, RFID_Reader/Writer.GND
  N7: U1.GPIO2, S1.Pin_1, S1.Pin_2, R5.Pin_0, C1.1
  N8: U1.GPIO4, S2.Pin_1, S2.Pin_2, R6.Pin_0, C2.1
  N9: U1.GPIO17, R1.Pin_0
  N10: U1.GPIO21, BME-280.SDA, OLED_128x64_I2C_-_1.SDA
  N11: U1.GPIO22, BME-280.SCL, OLED_128x64_I2C_-_1.SCK
  VDD: OLED_128x64_I2C_-_1.VDD, 9V_DC_/_5V_DC_Power_Supply.VCC#5, MQ-2.VCC
  N12: R4.Pin_0, LED3.cathode
  N13: Fan_12V.5V, 12V_DC_Power_Supply.+Vout
  N14: Fan_12V.GND, Q1.E
  N15: Q1.B, R1.Pin_1
  VCC: 9V_DC_/_5V_DC_Power_Supply.VCC#9, J1.vcc, OLED_128x64_I2C_-_2.VDD
  N16: LED2.cathode, R3.Pin_0
  N17: R2.Pin_0, LED1.cathode
  N18: J1.pulse, U2.GPIO13
  N19: Active_Buzzer_-_2.S, U2.GPIO12
  N20: OLED_128x64_I2C_-_2.SDA, U2.GPIO21
  N21: OLED_128x64_I2C_-_2.SCK, U2.GPIO22
  N22: RFID_Reader/Writer.NSS, U2.GPIO5
  N23: RFID_Reader/Writer.SCK, U2.GPIO18
  N24: RFID_Reader/Writer.MOSI, U2.GPIO23
  N25: RFID_Reader/Writer.MISO, U2.GPIO19
  N26: RFID_Reader/Writer.RST, U2.GPIO17
  N27: RFID_Reader/Writer.VCC, U2.3.3
  N28: R7.Pin_0, U2.GPIO25
  N29: R7.Pin_1, LED4.anode, LED5.anode, LED6.anode
  N30: U2.GND, LED4.cathode, LED5.cathode, LED6.cathode

custom parts:
  ESP32-38PinWide: Generic 38-Pin ESP32 with wide format (only access to one side of pins on a breadboard) based on Stephen Lilley's HiLetgo ESP-WROOM-32 ESP32 ESP-32S Development Board.
  Fan - Ventilador: Ventilador de 2 pines, se encuentra comunmente en computadoras de escritorio
  YwRobot Breadboard Power Supply: The YwRobot Breadboard Power Supply (MB-V2) has two power rails; they can be 5V or 3V3. Power to the module can be provided through the female USB socket or through the A10 (female) 2.1mm power jack.
  MQ-3 breakout: Alcohol sensor is capable of detecting alcohol (ethanol) particles on itself and gives the information in digital form back to us to manipulate with it. SKU:101251 • Voltage: 5V DC • Power: max 750mW • Measurement range: 0.04-4mg/L
  PowerBRICK 12V: PowerBRICKs are split-rail power supply modules that are intended to be used with a breadboard. These generate both a negative and positive voltage out of a single 5V USB voltage.
  KY-012 Active Buzzer Module: Active Piezoelectric Buzzer Module Keyes KY-012, it produces single-tone sound when signal is high.
  RFID RC522 Module: The RC522 is a 13.56MHz RFID module that is based on the MFRC522 controller from NXP semiconductors. The module can supports I2C, SPI and UART and normally is shipped with a RFID card and key fob. It is commonly used in attendance systems and other person/object identification applications.
